# Fritzing sketch ESP-Prayer-System (saved by Fritzing 1.0.4)
circuit board: 8.46667cm x 5.64444cm
breadboards: 1

parts:
  Mod1 = Amica NodeMCU DEVKIT 1.0
  DFRobot_DFPlayer_Mini1 = DFRobot DFPlayer Mini [part_number=DFR0299]
  J1 = Piezo Speaker
  Q1 = NPN-Transistor [package="TO92 [THT]"]
  Part1 = LCD1602-I2C
  RE1 = KY-040 Rotary encoder [package=THT]
  R1 = Resistor [tolerance=±5% power=0.25W resistance=1k package=THT]

nets:
  N1: Mod1.pin1, Mod1.pin_10, RE1.Vcc
  GND: Mod1.pin2, Mod1.pin_9, Mod1.pin_25, Mod1.pin_29, Q1.C, Part1.GND, RE1.GND
  N2: Mod1.pin5, RE1.DT
  N3: Mod1.pin6, RE1.CLK
  N4: Mod1.pin7, DFRobot_DFPlayer_Mini1.RX
  N5: Mod1.pin8, DFRobot_DFPlayer_Mini1.TX
  N6: Mod1.pin_11, RE1.SW
  N7: Mod1.pin_12, R1.Pin_1
  N8: Mod1.pin_14, Part1.SCL
  N9: Mod1.pin_30, J1.pin2, Part1.VCC
  N10: J1.pin1, Q1.E
  N11: Q1.B, R1.Pin_0

custom parts:
  LCD1602-I2C: A standard character display, usually with 2x16 characters. Comes in many colors with LCM1602 IIC attached.
  KY-040 Rotary encoder: KY-040 Rotary Encoder with switch on breakout borad from AZ Delivery
